# Fritzing sketch scheme (saved by Fritzing 0.9.3b)

parts:
  DHT1 = DHT11 Humitidy and Temperature Sensor
  Деталь1 = Arduino Mega 2560 (Rev3)

nets:
  VDD: DHT1.VDD, Деталь1.5V
  N1: DHT1.DATA, Деталь1.D30
  GND: DHT1.GND, Деталь1.GND

custom parts:
  DHT11 Humitidy and Temperature Sensor: DHT11 Humidity and Temperature Sensor
