# Fritzing sketch esp (saved by Fritzing 0.9.3b)

parts:
  U1 = NodeMCU V1.0
  Matrix_keypad1 = KEYPAD 4x4

nets:
  N1: U1.D0, Matrix_keypad1.row4
  N2: U1.D1, Matrix_keypad1.row3
  N3: U1.D2, Matrix_keypad1.row2
  N4: U1.D3, Matrix_keypad1.row1
  N5: U1.D4, Matrix_keypad1.col4
  N6: U1.D5, Matrix_keypad1.col3
  N7: U1.D7, Matrix_keypad1.col1

custom parts:
  NodeMCU V1.0: ESP8266 based NodeMCU
  KEYPAD 4x4: Matrix keypad 16 buttons, 4 rows x 4 columns
