# Fritzing sketch arduino (saved by Fritzing 0.9.3b)

parts:
  Part1 = Arduino Mega 2560 (Rev3)
  Part2 = HC-SR501 Body Sensor Module

nets:
  5V: Part1.5V, Part2.VCC
  GND: Part1.GND, Part2.GND
  N1: Part1.D31, Part2.OUT

custom parts:
  HC-SR501 Body Sensor Module: Pyroelectric Infrared PIR Motion Sensor Detector Module
