# Fritzing sketch arduino (saved by Fritzing 0.9.3b)

parts:
  Part1 = Arduino Mega 2560 (Rev3)
  DHT1 = DHT11 Humitidy and Temperature Sensor

nets:
  5V: Part1.5V, Part1.D30, DHT1.VDD, DHT1.DATA
  GND: Part1.GND, DHT1.GND

custom parts:
  DHT11 Humitidy and Temperature Sensor: DHT11 Humidity and Temperature Sensor
