# Fritzing sketch esp (saved by Fritzing 0.9.3b)

parts:
  U1 = NodeMCU V1.0
  DHT1 = DHT11 Humitidy and Temperature Sensor

nets:
  N1: U1.D1, DHT1.DATA
  GND: U1.GND, DHT1.GND
  VIN: U1.Vin, DHT1.VDD

custom parts:
  NodeMCU V1.0: ESP8266 based NodeMCU
  DHT11 Humitidy and Temperature Sensor: DHT11 Humidity and Temperature Sensor
