# Fritzing sketch scheme (saved by Fritzing 0.9.3b)

parts:
  Деталь1 = Arduino Mega 2560 (Rev3)
  ENC28J1 = ENC28J60

nets:
  5V: Деталь1.5V, ENC28J1.5v
  GND: Деталь1.GND, ENC28J1.GND
  N1: Деталь1.D50, ENC28J1.SO
  N2: Деталь1.D51, ENC28J1.SI
  N3: Деталь1.D52, ENC28J1.SCK, ENC28J1.RST
  N4: Деталь1.D53, ENC28J1.CS

custom parts:
  ENC28J60: Ethernet Module ENC28J60
